// Logisim project test.circ as structural Verilog: 1 circuit, main circuit main
module main (
  input  in_1,
  input  in_2
);

  wire undriven, undriven_2, xor_1_out;

  xor xor_1 (xor_1_out, undriven, undriven_2);
endmodule
